# Fritzing sketch board (saved by Fritzing 0.9.6b)
breadboards: 1

parts:
  WeMos_D1_Mini1 = WeMos D1 Mini  # not connected
  Part1 = Motor Driver 1A Dual TB6612FNG  # not connected
  IC1 = Voltage Regulator [package=to-92]
  Q1 = NPN-Transistor [package="SOT-23 [SMD]"]
  Q2 = NPN-Transistor [package="SOT-23 [SMD]"]
  R1 = Resistor [tolerance=±5% resistance=1k package="1206 [SMD]"]
  R2 = Resistor [tolerance=±5% resistance=1k package="1206 [SMD]"]
  R3 = Resistor [tolerance=±5% resistance=100 package="1206 [SMD]"]
  R4 = Resistor [tolerance=±5% resistance=100 package="1206 [SMD]"]
  J1 = Piezo Speaker
  IC2 = Voltage Regulator [package=to-92]

nets:
  N1: IC1.IN, J1.pin2
  N2: IC1.OUT, Q1.1, Q2.1, IC2.OUT
  N3: Q1.2, R3.Pin_0
  N4: Q1.0, R1.Pin_1
  N5: Q2.2, R4.Pin_0
  N6: Q2.0, R2.Pin_1
  N7: J1.pin1, IC2.GND

notes:
  Front lights
  Motor
  Servo
  Rear lights

custom parts:
  Voltage Regulator: voltage regulator
